# Fritzing sketch Switch-LED-Cooler__fritzing_ (saved by Fritzing 0.9.3b)
perfboards: 1

parts:
  Raspberry_Pi_1 = Raspberry Pi 3 [part_number=RPI-3-V1.2]
  S1 = Momentary Switch [package=ksa_sealed_tac_switch]
  R2 = Resistor [tolerance=±5% resistance=10k package="0402 [SMD]"]
  LED1 = DUO LED RG [package="5 mm [THT]"]  # not connected
  J3 = female pin header, 7 pins [form="♀ (female)"]  # not connected
  Fan_-_very_small1 = Little-Fan [package=THT]
  S3 = Toggle Switch [package=THT]

nets:
  N1: Raspberry_Pi_1.3v3, R2.Pin_0
  N2: Raspberry_Pi_1.GPIO3, S1.1, R2.Pin_1
  GND: Raspberry_Pi_1.GND, S1.2, Fan_-_very_small1.GND
  N3: Raspberry_Pi_1.5V, S3.COM
  N4: Fan_-_very_small1.5V, S3.L2

notes:
  Rot / Gün => LED Farbe
  kleiner PC-Lüfter zur Kühlung

custom parts:
  Little-Fan: Little PC-Fan with 2 pins
