# Fritzing sketch Switch-LED (saved by Fritzing 0.9.3b)

parts:
  Raspberry_Pi_1 = Raspberry Pi 3 [part_number=RPI-3-V1.2]
  LED1 = DUO LED RG [package="5 mm [THT]"]
  S2 = Momentary Switch [package=ksa_sealed_tac_switch]
  R3 = Resistor [tolerance=±5% resistance=10k package="0402 [SMD]"]

nets:
  N1: Raspberry_Pi_1.3v3, R3.Pin_1
  N2: Raspberry_Pi_1.GPIO3, S2.4, R3.Pin_0
  N3: Raspberry_Pi_1.GND, LED1.red_anode, S2.3
  N4: Raspberry_Pi_1.GPIO17, LED1.green_anode
  N5: Raspberry_Pi_1.GPIO27, LED1.common_cathode

notes:
  Red / Green => Dual-Color-Led
  Powerswitch
  with integrated Resistors
